// Logisim project cpu.circ as structural Verilog: 22 circuits, main circuit main
module main (
);

  wire and_1_out, and_2_out, Clear_out, Clock_out, ex_1_overflow, ex_1_zero, id_1_i_format, led_toggle_1_led,
       multi_d_ff_1_output_0, multi_d_ff_1_output_1, multi_d_ff_1_output_2, multi_d_ff_1_output_3,
       multi_d_ff_2_output_2, multi_d_ff_2_output_3, multi_d_ff_3_output_2, multi_d_ff_3_output_3,
       multi_d_ff_4_output_3, multi_d_ff_5_output_2, multi_d_ff_5_output_3, multi_d_ff_6_output_3,
       multi_d_ff_7_output_0, multi_d_ff_7_output_1, multi_d_ff_7_output_2, multi_d_ff_7_output_3,
       multi_d_ff_8_output_3, multi_d_ff_9_output_2, multi_d_ff_9_output_3, multi_d_ff_10_output_0,
       multi_d_ff_10_output_1, multi_d_ff_10_output_2, multi_d_ff_10_output_3, multi_d_ff_11_output_2,
       multi_d_ff_11_output_3, undriven, undriven_2, undriven_3, undriven_4, undriven_5, undriven_6,
       undriven_7, undriven_8, undriven_9, undriven_10, undriven_11, undriven_12, undriven_13, undriven_14,
       undriven_15, undriven_16, undriven_17, undriven_18, undriven_19, undriven_20, undriven_21,
       undriven_22, undriven_23, undriven_24;
  wire [1:0] id_1_aluop, id_1_ex, id_1_wb, multi_d_ff_2_output_0, multi_d_ff_3_output_0,
       multi_d_ff_5_output_0, multi_d_ff_9_output_0, multi_d_ff_11_output_0;
  wire [2:0] id_1_m, id_1_other, multi_d_ff_4_output_0, multi_d_ff_6_output_0, multi_d_ff_8_output_0;
  wire [4:0] n32_d_flip_flop_17_output;
  wire [7:0] n32_d_flip_flop_11_output_2;
  wire [23:0] n32_d_flip_flop_11_output;
  wire [26:0] n32_d_flip_flop_17_output_2;
  wire [31:0] adder_1_out, ex_1_result, ex_1_write_addr, id_1_instruction__15_0, id_1_instruction__15_11,
       id_1_instruction__20_16, id_1_instruction__25_0, id_1_instruction__31_26, id_1_read_data_1,
       id_1_read_data_2, if_1_instruction, if_1_pc__1, multiplexer_1_out, n32_d_flip_flop_1_output,
       n32_d_flip_flop_2_output, n32_d_flip_flop_3_output, n32_d_flip_flop_4_output,
       n32_d_flip_flop_5_output, n32_d_flip_flop_6_output, n32_d_flip_flop_7_output,
       n32_d_flip_flop_8_output, n32_d_flip_flop_10_output, n32_d_flip_flop_12_output,
       n32_d_flip_flop_13_output, n32_d_flip_flop_14_output, n32_d_flip_flop_15_output,
       n32_d_flip_flop_16_output, ram_1_data;

  Clock Clock (.out(Clock_out));
  IF if_1 (
    .Jump_Address(n32_d_flip_flop_12_output), .Jump(multi_d_ff_10_output_0), .PCSrc(and_2_out),
    .Clock(Clock_out), .Clear(undriven), .PC__1(if_1_pc__1), .Instruction(if_1_instruction));
  // Probe on if_1_instruction
  // Probe on if_1_pc__1
  _32_D_Flip_flop u_32_d_flip_flop_1 (
    .Input(if_1_pc__1), .Clock(Clock_out), .Clear(undriven_2), .Output(n32_d_flip_flop_1_output));
  _32_D_Flip_flop u_32_d_flip_flop_2 (
    .Input(if_1_instruction), .Clock(Clock_out), .Clear(undriven_2), .Output(n32_d_flip_flop_2_output));
  // Probe on n32_d_flip_flop_2_output
  ID id_1 (
    .Instruction(n32_d_flip_flop_2_output), .Write_Data(multiplexer_1_out),
    .Write_Reg(n32_d_flip_flop_17_output), .Write_Enable(multi_d_ff_11_output_0[1]), .Clear(undriven),
    .Clock(Clock_out), .Read_Data_1(id_1_read_data_1), .Read_Data_2(id_1_read_data_2),
    .Instruction__15_0(id_1_instruction__15_0), .Instruction__20_16(id_1_instruction__20_16),
    .Instruction__15_11(id_1_instruction__15_11), .Instruction__25_0(id_1_instruction__25_0),
    .Instruction__31_26(id_1_instruction__31_26), .I_Format(id_1_i_format), .ALUOp(id_1_aluop), .EX(id_1_ex),
    .M(id_1_m), .WB(id_1_wb), .Other(id_1_other));
  // Probe on n32_d_flip_flop_4_output
  _32_D_Flip_flop u_32_d_flip_flop_3 (
    .Input(n32_d_flip_flop_1_output), .Clock(Clock_out), .Clear(undriven_2), .Output(n32_d_flip_flop_3_output));
  _32_D_Flip_flop u_32_d_flip_flop_4 (
    .Input(id_1_read_data_1), .Clock(Clock_out), .Clear(undriven_2), .Output(n32_d_flip_flop_4_output));
  _32_D_Flip_flop u_32_d_flip_flop_5 (
    .Input(id_1_read_data_2), .Clock(Clock_out), .Clear(undriven_2), .Output(n32_d_flip_flop_5_output));
  _32_D_Flip_flop u_32_d_flip_flop_6 (
    .Input(id_1_instruction__15_0), .Clock(Clock_out), .Clear(undriven_2), .Output(n32_d_flip_flop_6_output));
  _32_D_Flip_flop u_32_d_flip_flop_7 (
    .Input(id_1_instruction__20_16), .Clock(Clock_out), .Clear(undriven_2), .Output(n32_d_flip_flop_7_output));
  _32_D_Flip_flop u_32_d_flip_flop_8 (
    .Input(id_1_instruction__15_11), .Clock(Clock_out), .Clear(undriven_2), .Output(n32_d_flip_flop_8_output));
  _32_D_Flip_flop u_32_d_flip_flop_9 (
    .Input(id_1_instruction__25_0), .Clock(Clock_out), .Clear(undriven_2));  // open: Output
  _32_D_Flip_flop u_32_d_flip_flop_10 (
    .Input(id_1_instruction__31_26), .Clock(Clock_out), .Clear(undriven_2), .Output(n32_d_flip_flop_10_output));
  Multi_D_Flip_Flop multi_d_ff_1 (
    .Mask(4'b0001), .Input_0(id_1_i_format), .Input_1(undriven_3), .Input_2(undriven_4),
    .Input_3(undriven_5), .Clock(Clock_out), .Clear(undriven_2), .Output_0(multi_d_ff_1_output_0),
    .Output_1(multi_d_ff_1_output_1), .Output_2(multi_d_ff_1_output_2), .Output_3(multi_d_ff_1_output_3));
  Multi_D_Flip_Flop multi_d_ff_2 (
    .Mask(4'b0011), .Input_0(id_1_aluop[0]), .Input_1(id_1_aluop[1]), .Input_2(undriven_6),
    .Input_3(undriven_7), .Clock(Clock_out), .Clear(undriven_2), .Output_0(multi_d_ff_2_output_0[0]),
    .Output_1(multi_d_ff_2_output_0[1]), .Output_2(multi_d_ff_2_output_2), .Output_3(multi_d_ff_2_output_3));
  Multi_D_Flip_Flop multi_d_ff_3 (
    .Mask(4'b0011), .Input_0(id_1_ex[0]), .Input_1(id_1_ex[1]), .Input_2(undriven_8), .Input_3(undriven_9),
    .Clock(Clock_out), .Clear(undriven_2), .Output_0(multi_d_ff_3_output_0[0]),
    .Output_1(multi_d_ff_3_output_0[1]), .Output_2(multi_d_ff_3_output_2), .Output_3(multi_d_ff_3_output_3));
  Multi_D_Flip_Flop multi_d_ff_4 (
    .Mask(4'b0111), .Input_0(id_1_m[0]), .Input_1(id_1_m[1]), .Input_2(id_1_m[2]), .Input_3(undriven_10),
    .Clock(Clock_out), .Clear(undriven_2), .Output_0(multi_d_ff_4_output_0[0]),
    .Output_1(multi_d_ff_4_output_0[1]), .Output_2(multi_d_ff_4_output_0[2]), .Output_3(multi_d_ff_4_output_3));
  Multi_D_Flip_Flop multi_d_ff_5 (
    .Mask(4'b0011), .Input_0(id_1_wb[0]), .Input_1(id_1_wb[1]), .Input_2(undriven_11), .Input_3(undriven_12),
    .Clock(Clock_out), .Clear(undriven_2), .Output_0(multi_d_ff_5_output_0[0]),
    .Output_1(multi_d_ff_5_output_0[1]), .Output_2(multi_d_ff_5_output_2), .Output_3(multi_d_ff_5_output_3));
  Multi_D_Flip_Flop multi_d_ff_6 (
    .Mask(4'b0111), .Input_0(id_1_other[0]), .Input_1(id_1_other[1]), .Input_2(id_1_other[2]),
    .Input_3(undriven_13), .Clock(Clock_out), .Clear(undriven_2), .Output_0(multi_d_ff_6_output_0[0]),
    .Output_1(multi_d_ff_6_output_0[1]), .Output_2(multi_d_ff_6_output_0[2]), .Output_3(multi_d_ff_6_output_3));
  // Probe on n32_d_flip_flop_5_output
  // Probe on multi_d_ff_2_output_0
  // Probe on ex_1_result
  EX ex_1 (
    .Read_Data_1(n32_d_flip_flop_4_output), .Read_Data_2(n32_d_flip_flop_5_output),
    .Instruction__15_0(n32_d_flip_flop_6_output), .Instruction__20_16(n32_d_flip_flop_7_output),
    .Instruction__15_11(n32_d_flip_flop_8_output), .Instruction__31_26(n32_d_flip_flop_10_output),
    .ALUOp(multi_d_ff_2_output_0), .EX(multi_d_ff_3_output_0), .Signed(multi_d_ff_6_output_0[0]),
    .I_Format(multi_d_ff_1_output_0), .Result(ex_1_result), .Zero(ex_1_zero), .Overflow(ex_1_overflow),
    .Write_Addr(ex_1_write_addr));
  LED ALU_Overflow (.in(led_toggle_1_led));
  Button Clear (.out(Clear_out));
  and and_1 (and_1_out, ex_1_zero, multi_d_ff_6_output_0[1]);
  LED_Toggle led_toggle_1 (.Reset(Clear_out), .LED(led_toggle_1_led), .Input(ex_1_overflow));
  Adder #(.width(32)) adder_1 (
    .a(n32_d_flip_flop_3_output), .b({n32_d_flip_flop_6_output[29:0], 2'b00}), .out(adder_1_out));  // open: cin, cout
  _32_D_Flip_flop u_32_d_flip_flop_11 (
    .Input(ex_1_result), .Clock(Clock_out), .Clear(undriven_2),
    .Output({n32_d_flip_flop_11_output_2, n32_d_flip_flop_11_output}));
  Multi_D_Flip_Flop multi_d_ff_7 (
    .Mask(4'b0001), .Input_0(and_1_out), .Input_1(undriven_14), .Input_2(undriven_15), .Input_3(undriven_16),
    .Clock(Clock_out), .Clear(undriven_2), .Output_0(multi_d_ff_7_output_0),
    .Output_1(multi_d_ff_7_output_1), .Output_2(multi_d_ff_7_output_2), .Output_3(multi_d_ff_7_output_3));
  _32_D_Flip_flop u_32_d_flip_flop_12 (
    .Input(adder_1_out), .Clock(Clock_out), .Clear(undriven_2), .Output(n32_d_flip_flop_12_output));
  _32_D_Flip_flop u_32_d_flip_flop_13 (
    .Input(n32_d_flip_flop_4_output), .Clock(Clock_out), .Clear(undriven_2),
    .Output(n32_d_flip_flop_13_output));
  _32_D_Flip_flop u_32_d_flip_flop_14 (
    .Input(ex_1_write_addr), .Clock(Clock_out), .Clear(undriven_2), .Output(n32_d_flip_flop_14_output));
  Multi_D_Flip_Flop multi_d_ff_8 (
    .Mask(4'b0111), .Input_0(multi_d_ff_4_output_0[0]), .Input_1(multi_d_ff_4_output_0[1]),
    .Input_2(multi_d_ff_4_output_0[2]), .Input_3(undriven_17), .Clock(Clock_out), .Clear(undriven_2),
    .Output_0(multi_d_ff_8_output_0[0]), .Output_1(multi_d_ff_8_output_0[1]),
    .Output_2(multi_d_ff_8_output_0[2]), .Output_3(multi_d_ff_8_output_3));
  Multi_D_Flip_Flop multi_d_ff_9 (
    .Mask(4'b0011), .Input_0(multi_d_ff_5_output_0[0]), .Input_1(multi_d_ff_5_output_0[1]),
    .Input_2(undriven_18), .Input_3(undriven_19), .Clock(Clock_out), .Clear(undriven_2),
    .Output_0(multi_d_ff_9_output_0[0]), .Output_1(multi_d_ff_9_output_0[1]),
    .Output_2(multi_d_ff_9_output_2), .Output_3(multi_d_ff_9_output_3));
  Multi_D_Flip_Flop multi_d_ff_10 (
    .Mask(4'b0001), .Input_0(multi_d_ff_6_output_0[2]), .Input_1(undriven_20), .Input_2(undriven_21),
    .Input_3(undriven_22), .Output_0(multi_d_ff_10_output_0), .Output_1(multi_d_ff_10_output_1),
    .Output_2(multi_d_ff_10_output_2), .Output_3(multi_d_ff_10_output_3));  // open: Clock, Clear
  and and_2 (and_2_out, multi_d_ff_7_output_0, multi_d_ff_8_output_0[0]);
  // Probe on n32_d_flip_flop_11_output
  // Probe on n32_d_flip_flop_13_output
  // Probe on multiplexer_1_out
  RAM #(.addrWidth(24), .dataWidth(32), .bus("separate")) ram_1 (
    .addr(n32_d_flip_flop_11_output), .din(n32_d_flip_flop_13_output), .data(ram_1_data),
    .str(multi_d_ff_8_output_0[2]), .sel(1'b1), .clk(Clock_out), .ld(multi_d_ff_8_output_0[1]), .clr(undriven));
  // Probe on n32_d_flip_flop_17_output
  _32_D_Flip_flop u_32_d_flip_flop_15 (
    .Input(ram_1_data), .Clock(Clock_out), .Clear(undriven_2), .Output(n32_d_flip_flop_15_output));
  _32_D_Flip_flop u_32_d_flip_flop_16 (
    .Input({n32_d_flip_flop_11_output_2, n32_d_flip_flop_11_output}), .Clock(Clock_out), .Clear(undriven_2),
    .Output(n32_d_flip_flop_16_output));
  _32_D_Flip_flop u_32_d_flip_flop_17 (
    .Input(n32_d_flip_flop_14_output), .Clock(Clock_out), .Clear(undriven_2),
    .Output({n32_d_flip_flop_17_output_2, n32_d_flip_flop_17_output}));
  Multi_D_Flip_Flop multi_d_ff_11 (
    .Mask(4'b0011), .Input_0(multi_d_ff_9_output_0[0]), .Input_1(multi_d_ff_9_output_0[1]),
    .Input_2(undriven_23), .Input_3(undriven_24), .Clock(Clock_out), .Clear(undriven_2),
    .Output_0(multi_d_ff_11_output_0[0]), .Output_1(multi_d_ff_11_output_0[1]),
    .Output_2(multi_d_ff_11_output_2), .Output_3(multi_d_ff_11_output_3));
  Multiplexer #(.width(32), .enable("false")) multiplexer_1 (
    .in0(n32_d_flip_flop_16_output), .in1(n32_d_flip_flop_15_output), .out(multiplexer_1_out),
    .sel(multi_d_ff_11_output_0[0]));

  // Notes on the sheet:
  //   IF/ID
  //   ID/EX
  //   Signed
  //   BEQ/BNE
  //   Jump
  //   EX/MEM
  //   PCSrc
  //   Jump
  //   MEM/WB
  //   RegWrite
  //   MemtoReg
endmodule

// (32)
module _32_D_Flip_flop (
  input  Clock,
  input  [31:0] Input,
  input  Clear,
  output [31:0] Output
);

  D_Flip_Flop d_ff_1 (.clk(Clock), .D(Input[24]), .Q(Output[24]), .reset(Clear));  // open: Qn, preset, en
  D_Flip_Flop d_ff_2 (.clk(Clock), .D(Input[25]), .Q(Output[25]), .reset(Clear));  // open: Qn, preset, en
  D_Flip_Flop d_ff_3 (.clk(Clock), .D(Input[26]), .Q(Output[26]), .reset(Clear));  // open: Qn, preset, en
  D_Flip_Flop d_ff_4 (.clk(Clock), .D(Input[27]), .Q(Output[27]), .reset(Clear));  // open: Qn, preset, en
  D_Flip_Flop d_ff_5 (.clk(Clock), .D(Input[28]), .Q(Output[28]), .reset(Clear));  // open: Qn, preset, en
  D_Flip_Flop d_ff_6 (.clk(Clock), .D(Input[29]), .Q(Output[29]), .reset(Clear));  // open: Qn, preset, en
  D_Flip_Flop d_ff_7 (.clk(Clock), .D(Input[30]), .Q(Output[30]), .reset(Clear));  // open: Qn, preset, en
  D_Flip_Flop d_ff_8 (.clk(Clock), .D(Input[31]), .Q(Output[31]), .reset(Clear));  // open: Qn, preset, en
  D_Flip_Flop d_ff_9 (.clk(Clock), .D(Input[16]), .Q(Output[16]), .reset(Clear));  // open: Qn, preset, en
  D_Flip_Flop d_ff_10 (.clk(Clock), .D(Input[17]), .Q(Output[17]), .reset(Clear));  // open: Qn, preset, en
  D_Flip_Flop d_ff_11 (.clk(Clock), .D(Input[18]), .Q(Output[18]), .reset(Clear));  // open: Qn, preset, en
  D_Flip_Flop d_ff_12 (.clk(Clock), .D(Input[19]), .Q(Output[19]), .reset(Clear));  // open: Qn, preset, en
  D_Flip_Flop d_ff_13 (.clk(Clock), .D(Input[20]), .Q(Output[20]), .reset(Clear));  // open: Qn, preset, en
  D_Flip_Flop d_ff_14 (.clk(Clock), .D(Input[21]), .Q(Output[21]), .reset(Clear));  // open: Qn, preset, en
  D_Flip_Flop d_ff_15 (.clk(Clock), .D(Input[22]), .Q(Output[22]), .reset(Clear));  // open: Qn, preset, en
  D_Flip_Flop d_ff_16 (.clk(Clock), .D(Input[23]), .Q(Output[23]), .reset(Clear));  // open: Qn, preset, en
  D_Flip_Flop d_ff_17 (.clk(Clock), .D(Input[8]), .Q(Output[8]), .reset(Clear));  // open: Qn, preset, en
  D_Flip_Flop d_ff_18 (.clk(Clock), .D(Input[9]), .Q(Output[9]), .reset(Clear));  // open: Qn, preset, en
  D_Flip_Flop d_ff_19 (.clk(Clock), .D(Input[10]), .Q(Output[10]), .reset(Clear));  // open: Qn, preset, en
  D_Flip_Flop d_ff_20 (.clk(Clock), .D(Input[11]), .Q(Output[11]), .reset(Clear));  // open: Qn, preset, en
  D_Flip_Flop d_ff_21 (.clk(Clock), .D(Input[12]), .Q(Output[12]), .reset(Clear));  // open: Qn, preset, en
  D_Flip_Flop d_ff_22 (.clk(Clock), .D(Input[13]), .Q(Output[13]), .reset(Clear));  // open: Qn, preset, en
  D_Flip_Flop d_ff_23 (.clk(Clock), .D(Input[14]), .Q(Output[14]), .reset(Clear));  // open: Qn, preset, en
  D_Flip_Flop d_ff_24 (.clk(Clock), .D(Input[15]), .Q(Output[15]), .reset(Clear));  // open: Qn, preset, en
  D_Flip_Flop d_ff_25 (.clk(Clock), .D(Input[0]), .Q(Output[0]), .reset(Clear));  // open: Qn, preset, en
  D_Flip_Flop d_ff_26 (.clk(Clock), .D(Input[1]), .Q(Output[1]), .reset(Clear));  // open: Qn, preset, en
  D_Flip_Flop d_ff_27 (.clk(Clock), .D(Input[2]), .Q(Output[2]), .reset(Clear));  // open: Qn, preset, en
  D_Flip_Flop d_ff_28 (.clk(Clock), .D(Input[3]), .Q(Output[3]), .reset(Clear));  // open: Qn, preset, en
  D_Flip_Flop d_ff_29 (.clk(Clock), .D(Input[4]), .Q(Output[4]), .reset(Clear));  // open: Qn, preset, en
  D_Flip_Flop d_ff_30 (.clk(Clock), .D(Input[5]), .Q(Output[5]), .reset(Clear));  // open: Qn, preset, en
  D_Flip_Flop d_ff_31 (.clk(Clock), .D(Input[6]), .Q(Output[6]), .reset(Clear));  // open: Qn, preset, en
  D_Flip_Flop d_ff_32 (.clk(Clock), .D(Input[7]), .Q(Output[7]), .reset(Clear));  // open: Qn, preset, en
endmodule

// (Var)
module Multi_D_Flip_Flop (
  input  Clock,
  input  Clear,
  input  [3:0] Mask,
  input  Input_0,
  input  Input_1,
  input  Input_2,
  input  Input_3,
  output Output_0,
  output Output_1,
  output Output_2,
  output Output_3
);

  wire d_ff_1_q, d_ff_2_q, d_ff_3_q, d_ff_4_q;

  D_Flip_Flop d_ff_1 (.clk(Clock), .D(Input_0), .Q(d_ff_1_q), .reset(Clear));  // open: Qn, preset, en
  D_Flip_Flop d_ff_2 (.clk(Clock), .D(Input_1), .Q(d_ff_2_q), .reset(Clear));  // open: Qn, preset, en
  D_Flip_Flop d_ff_3 (.clk(Clock), .D(Input_2), .Q(d_ff_3_q), .reset(Clear));  // open: Qn, preset, en
  D_Flip_Flop d_ff_4 (.clk(Clock), .D(Input_3), .Q(d_ff_4_q), .reset(Clear));  // open: Qn, preset, en
  and and_1 (Output_0, d_ff_1_q, Mask[0]);
  and and_2 (Output_1, Mask[1], d_ff_2_q);
  and and_3 (Output_2, Mask[2], d_ff_3_q);
  and and_4 (Output_3, Mask[3], d_ff_4_q);
endmodule

module IF (
  input  PCSrc,
  input  [31:0] Jump_Address,
  input  Jump,
  input  Clock,
  input  Clear,
  output [31:0] PC__1,
  output [31:0] Instruction
);

  wire [31:0] multiplexer_1_out, multiplexer_2_out, pc_1_instruction_address;

  Multiplexer #(.width(32), .enable("false")) multiplexer_1 (
    .in0(PC__1), .in1(Jump_Address), .out(multiplexer_1_out), .sel(PCSrc));
  Multiplexer #(.width(32), .enable("false")) multiplexer_2 (
    .in0(multiplexer_1_out), .in1(Jump_Address), .out(multiplexer_2_out), .sel(Jump));
  PC pc_1 (
    .Next_Address(multiplexer_2_out), .Clock(Clock), .Clear(Clear),
    .Instruction_Address(pc_1_instruction_address));
  IM im_1 (.Address(pc_1_instruction_address), .Instruction(Instruction));
  Adder #(.width(32)) adder_1 (.a(pc_1_instruction_address), .b(32'h1), .out(PC__1));  // open: cin, cout
endmodule

module PC (
  input  Clock,
  input  Clear,
  input  [31:0] Next_Address,
  output [31:0] Instruction_Address
);

  _32_D_Flip_flop u_32_d_flip_flop_1 (.Input(Next_Address), .Clock(Clock), .Clear(Clear), .Output(Instruction_Address));
endmodule

module IM (
  input  [31:0] Address,
  output [31:0] Instruction
);

  ROM #(.addrWidth(24), .dataWidth(32)) rom_1 (.addr(Address[23:0]), .data(Instruction), .sel(1'b1));

  // Notes on the sheet:
  //   contents of rom_1 (hex, n*v repeats v):
  //   8c210000
endmodule

module ID (
  input  Clear,
  input  Clock,
  input  [31:0] Instruction,
  input  [31:0] Write_Data,
  input  [4:0] Write_Reg,
  input  Write_Enable,
  output [31:0] Read_Data_1,
  output [31:0] Read_Data_2,
  output [31:0] Instruction__15_0,
  output [31:0] Instruction__20_16,
  output [31:0] Instruction__15_11,
  output [31:0] Instruction__25_0,
  output [31:0] Instruction__31_26,
  output I_Format,
  output [1:0] ALUOp,
  output [1:0] EX,
  output [2:0] M,
  output [1:0] WB,
  output [2:0] Other
);

  wire [4:0] decoder_1__25_21;
  wire [15:0] decoder_1__15_0;

  Decoder decoder_1 (
    .Instruction(Instruction), ._11_15(Instruction__15_11[4:0]), ._15_0(decoder_1__15_0),
    ._20_16(Instruction__20_16[4:0]), ._25_21(decoder_1__25_21), ._31_26(Instruction__31_26[5:0]),
    ._25_0(Instruction__25_0));
  Registers registers_1 (
    .Clock(Clock), .Enable_1(1'b1), .Read_Reg_1(Instruction__20_16[4:0]), .Enable_2(1'b1),
    .Read_Reg_2(decoder_1__25_21), .Enable_Write(Write_Enable), .Write_Reg(Write_Reg),
    .Write_Data(Write_Data), .Clear_All(Clear), .Read_Data_1(Read_Data_1), .Read_Data_2(Read_Data_2));
  assign Instruction__15_0 = {{16{decoder_1__15_0[15]}}, decoder_1__15_0};  // Bit_Extender bit_extender_1
  Control control_1 (
    .Instruction__31_26(Instruction__31_26[5:0]), .I_Format(I_Format), .ALUOp(ALUOp), .EX(EX), .M(M),
    .WB(WB), .Other(Other));

  assign Instruction__15_11[31:5] = {27{1'b0}};
  assign Instruction__20_16[31:5] = {27{1'b0}};
  assign Instruction__31_26[31:6] = {26{1'b0}};
endmodule

module Decoder (
  input  [31:0] Instruction,
  output [4:0] _11_15,
  output [15:0] _15_0,
  output [4:0] _20_16,
  output [4:0] _25_21,
  output [5:0] _31_26,
  output [31:0] _25_0
);


  assign _11_15 = Instruction[15:11];
  assign _15_0 = Instruction[15:0];
  assign _20_16 = Instruction[20:16];
  assign _25_0 = {{6{1'b0}}, Instruction[25:0]};
  assign _25_21 = Instruction[25:21];
  assign _31_26 = Instruction[31:26];
endmodule

module Registers (
  input  Clock,
  input  Enable_1,
  input  [4:0] Read_Reg_1,
  input  Enable_2,
  input  [4:0] Read_Reg_2,
  input  Enable_Write,
  input  [4:0] Write_Reg,
  input  [31:0] Write_Data,
  input  Clear_All,
  output [31:0] Read_Data_1,
  output [31:0] Read_Data_2
);

  wire and_1_out, and_2_out, and_3_out, demultiplexer_1_out0, demultiplexer_1_out1, demultiplexer_1_out2,
       demultiplexer_1_out3, demultiplexer_1_out4, demultiplexer_1_out5, demultiplexer_1_out6,
       demultiplexer_1_out7, demultiplexer_2_out0, demultiplexer_2_out1, demultiplexer_2_out2,
       demultiplexer_2_out3, demultiplexer_2_out4, demultiplexer_2_out5, demultiplexer_2_out6,
       demultiplexer_2_out7, nor_1_out, nor_2_out, or_1_out;
  wire [1:0] controlled_buffer_1_out, controlled_buffer_2_out, n32_8_split_1_remainder,
       n32_8_split_2_remainder;
  wire [2:0] n32_8_split_1_output, n32_8_split_2_output;
  wire [4:0] multiplexer_1_out;
  wire [31:0] n4_register_1_out_1, n4_register_1_out_2;

  or or_1 (or_1_out, Enable_1, Enable_Write);
  and and_1 (and_1_out, Clock, Enable_Write);
  _32_8_Split u_32_8_split_1 (
    .Input(multiplexer_1_out), .Output(n32_8_split_1_output), .Remainder(n32_8_split_1_remainder));
  Multiplexer #(.width(5), .enable("false")) multiplexer_1 (
    .in0(Read_Reg_1), .in1(Write_Reg), .out(multiplexer_1_out), .sel(Enable_Write));
  _32_8_Split u_32_8_split_2 (.Input(Read_Reg_2), .Output(n32_8_split_2_output), .Remainder(n32_8_split_2_remainder));
  and and_2 (and_2_out, Enable_2, nor_1_out);
  nor nor_1 (nor_1_out, Read_Reg_2[0], Read_Reg_2[1], Read_Reg_2[2], Read_Reg_2[3], Read_Reg_2[4]);
  and and_3 (and_3_out, Enable_1, nor_2_out);
  nor nor_2 (nor_2_out, Read_Reg_1[0], Read_Reg_1[1], Read_Reg_1[2], Read_Reg_1[3], Read_Reg_1[4]);
  Demultiplexer #(.select(3), .enable("false")) demultiplexer_1 (
    .out0(demultiplexer_1_out0), .out1(demultiplexer_1_out1), .out2(demultiplexer_1_out2),
    .out3(demultiplexer_1_out3), .out4(demultiplexer_1_out4), .out5(demultiplexer_1_out5),
    .out6(demultiplexer_1_out6), .out7(demultiplexer_1_out7), .in(or_1_out), .sel(n32_8_split_1_output));
  Demultiplexer #(.select(3), .enable("false")) demultiplexer_2 (
    .out0(demultiplexer_2_out0), .out1(demultiplexer_2_out1), .out2(demultiplexer_2_out2),
    .out3(demultiplexer_2_out3), .out4(demultiplexer_2_out4), .out5(demultiplexer_2_out5),
    .out6(demultiplexer_2_out6), .out7(demultiplexer_2_out7), .in(Enable_2), .sel(n32_8_split_2_output));
  assign controlled_buffer_1_out = or_1_out ? n32_8_split_1_remainder : 2'bz;  // Controlled_Buffer controlled_buffer_1
  assign controlled_buffer_2_out = Enable_2 ? n32_8_split_2_remainder : 2'bz;  // Controlled_Buffer controlled_buffer_2
  _4_Register u_4_register_1 (
    .Clock(and_1_out), .Clear_All(Clear_All), .Data_In(Write_Data),
    .Register_Addr_1(controlled_buffer_1_out), .Enable_1(demultiplexer_1_out0),
    .Register_Addr_2(controlled_buffer_2_out), .Enable_2(demultiplexer_2_out0), .Out_1(n4_register_1_out_1),
    .Out_2(n4_register_1_out_2));
  _4_Register u_4_register_2 (
    .Clock(and_1_out), .Clear_All(Clear_All), .Data_In(Write_Data),
    .Register_Addr_1(controlled_buffer_1_out), .Enable_1(demultiplexer_1_out1),
    .Register_Addr_2(controlled_buffer_2_out), .Enable_2(demultiplexer_2_out1), .Out_1(n4_register_1_out_1),
    .Out_2(n4_register_1_out_2));
  _4_Register u_4_register_3 (
    .Clock(and_1_out), .Clear_All(Clear_All), .Data_In(Write_Data),
    .Register_Addr_1(controlled_buffer_1_out), .Enable_1(demultiplexer_1_out2),
    .Register_Addr_2(controlled_buffer_2_out), .Enable_2(demultiplexer_2_out2), .Out_1(n4_register_1_out_1),
    .Out_2(n4_register_1_out_2));
  _4_Register u_4_register_4 (
    .Clock(and_1_out), .Clear_All(Clear_All), .Data_In(Write_Data),
    .Register_Addr_1(controlled_buffer_1_out), .Enable_1(demultiplexer_1_out3),
    .Register_Addr_2(controlled_buffer_2_out), .Enable_2(demultiplexer_2_out3), .Out_1(n4_register_1_out_1),
    .Out_2(n4_register_1_out_2));
  _4_Register u_4_register_5 (
    .Clock(and_1_out), .Clear_All(Clear_All), .Data_In(Write_Data),
    .Register_Addr_1(controlled_buffer_1_out), .Enable_1(demultiplexer_1_out4),
    .Register_Addr_2(controlled_buffer_2_out), .Enable_2(demultiplexer_2_out4), .Out_1(n4_register_1_out_1),
    .Out_2(n4_register_1_out_2));
  _4_Register u_4_register_6 (
    .Clock(and_1_out), .Clear_All(Clear_All), .Data_In(Write_Data),
    .Register_Addr_1(controlled_buffer_1_out), .Enable_1(demultiplexer_1_out5),
    .Register_Addr_2(controlled_buffer_2_out), .Enable_2(demultiplexer_2_out5), .Out_1(n4_register_1_out_1),
    .Out_2(n4_register_1_out_2));
  _4_Register u_4_register_7 (
    .Clock(and_1_out), .Clear_All(Clear_All), .Data_In(Write_Data),
    .Register_Addr_1(controlled_buffer_1_out), .Enable_1(demultiplexer_1_out6),
    .Register_Addr_2(controlled_buffer_2_out), .Enable_2(demultiplexer_2_out6), .Out_1(n4_register_1_out_1),
    .Out_2(n4_register_1_out_2));
  _4_Register u_4_register_8 (
    .Clock(and_1_out), .Clear_All(Clear_All), .Data_In(Write_Data),
    .Register_Addr_1(controlled_buffer_1_out), .Enable_1(demultiplexer_1_out7),
    .Register_Addr_2(controlled_buffer_2_out), .Enable_2(demultiplexer_2_out7), .Out_1(n4_register_1_out_1),
    .Out_2(n4_register_1_out_2));
  Multiplexer #(.width(32), .enable("false")) multiplexer_2 (
    .in0(n4_register_1_out_1), .in1({32{1'b0}}), .out(Read_Data_1), .sel(and_3_out));
  Multiplexer #(.width(32), .enable("false")) multiplexer_3 (
    .in0(n4_register_1_out_2), .in1({32{1'b0}}), .out(Read_Data_2), .sel(and_2_out));

  // Notes on the sheet:
  //   $Zero
endmodule

module _32_8_Split (
  input  [4:0] Input,
  output [2:0] Output,
  output [1:0] Remainder
);


  assign Output = Input[4:2];
  assign Remainder = Input[1:0];
endmodule

module _4_Register (
  input  Clock,
  input  Clear_All,
  input  [31:0] Data_In,
  input  [1:0] Register_Addr_1,
  input  Enable_1,
  input  [1:0] Register_Addr_2,
  input  Enable_2,
  output [31:0] Out_1,
  output [31:0] Out_2
);

  wire and_1_out, and_2_out, and_3_out, and_4_out, demultiplexer_1_out0, demultiplexer_1_out1,
       demultiplexer_1_out2, demultiplexer_1_out3, demultiplexer_2_out0, demultiplexer_2_out1,
       demultiplexer_2_out2, demultiplexer_2_out3, or_1_out, or_2_out, or_3_out, or_4_out;
  wire [31:0] multiplexer_1_out, multiplexer_2_out, register_1_q, register_2_q, register_3_q, register_4_q;

  Demultiplexer #(.select(2), .enable("false")) demultiplexer_1 (
    .out0(demultiplexer_1_out0), .out1(demultiplexer_1_out1), .out2(demultiplexer_1_out2),
    .out3(demultiplexer_1_out3), .in(Enable_1), .sel(Register_Addr_1));
  Demultiplexer #(.select(2), .enable("false")) demultiplexer_2 (
    .out0(demultiplexer_2_out0), .out1(demultiplexer_2_out1), .out2(demultiplexer_2_out2),
    .out3(demultiplexer_2_out3), .in(Enable_2), .sel(Register_Addr_2));
  or or_1 (or_1_out, demultiplexer_1_out0, demultiplexer_2_out0);
  or or_2 (or_2_out, demultiplexer_1_out1, demultiplexer_2_out1);
  or or_3 (or_3_out, demultiplexer_1_out2, demultiplexer_2_out2);
  or or_4 (or_4_out, demultiplexer_1_out3, demultiplexer_2_out3);
  Register #(.width(32)) register_1 (.D(Data_In), .en(or_1_out), .Q(register_1_q), .clk(and_1_out), .clr(Clear_All));
  and and_1 (and_1_out, or_1_out, Clock);
  and and_2 (and_2_out, or_2_out, Clock);
  Register #(.width(32)) register_2 (.D(Data_In), .en(or_2_out), .Q(register_2_q), .clk(and_2_out), .clr(Clear_All));
  and and_3 (and_3_out, or_3_out, Clock);
  Register #(.width(32)) register_3 (.D(Data_In), .en(or_4_out), .Q(register_3_q), .clk(and_4_out), .clr(Clear_All));
  Register #(.width(32)) register_4 (.D(Data_In), .en(or_3_out), .Q(register_4_q), .clk(and_3_out), .clr(Clear_All));
  and and_4 (and_4_out, or_4_out, Clock);
  Multiplexer #(.select(2), .width(32), .enable("false")) multiplexer_1 (
    .in0(register_1_q), .in1(register_2_q), .in2(register_4_q), .in3(register_3_q), .out(multiplexer_1_out),
    .sel(Register_Addr_1));
  Multiplexer #(.select(2), .width(32), .enable("false")) multiplexer_2 (
    .in0(register_1_q), .in1(register_2_q), .in2(register_4_q), .in3(register_3_q), .out(multiplexer_2_out),
    .sel(Register_Addr_2));
  assign Out_1 = Enable_1 ? multiplexer_1_out : 32'bz;  // Controlled_Buffer controlled_buffer_1
  assign Out_2 = Enable_2 ? multiplexer_2_out : 32'bz;  // Controlled_Buffer controlled_buffer_2
endmodule

module EX (
  input  [31:0] Read_Data_1,
  input  [31:0] Read_Data_2,
  input  [31:0] Instruction__15_0,
  input  [31:0] Instruction__20_16,
  input  [31:0] Instruction__15_11,
  input  [31:0] Instruction__31_26,
  input  [1:0] ALUOp,
  input  [1:0] EX,
  input  Signed,
  input  I_Format,
  output [31:0] Result,
  output Zero,
  output Overflow,
  output [31:0] Write_Addr
);

  wire alu_1_overflow, alu_decoder_1_signed, and_1_out, M_D_out, MF_H_L_out, or_1_out, or_2_out;
  wire [2:0] alu_decoder_1_destination_unit;
  wire [3:0] alu_decoder_1_operation;
  wire [31:0] alu_1_result, HI_q, LO_q, mdlu_1_hi, mdlu_1_lo, multiplexer_1_out, multiplexer_3_out,
       slu_1_output;

  Multiplexer #(.width(32), .enable("false")) multiplexer_1 (
    .in0(Read_Data_2), .in1(Instruction__15_0), .out(multiplexer_1_out), .sel(EX[0]));
  ALU_Decoder alu_decoder_1 (
    .Funct__5_0(Instruction__15_0[5:0]), .I_Format(I_Format), .Instruction__31_26(Instruction__31_26),
    .Operation(alu_decoder_1_operation), .Signed(alu_decoder_1_signed),
    .Destination_Unit(alu_decoder_1_destination_unit));
  Multiplexer #(.width(32), .enable("false")) multiplexer_2 (
    .in0(Instruction__20_16), .in1(Instruction__15_11), .out(Write_Addr), .sel(EX[1]));
  or or_1 (or_1_out, alu_decoder_1_signed, Signed);
  ALU alu_1 (
    .OPCode(alu_decoder_1_operation), .Input_1(Read_Data_1), .Input_2(multiplexer_1_out),
    .Result(alu_1_result), .Overflow(alu_1_overflow));
  SLU slu_1 (
    .OPCode(alu_decoder_1_operation), .Signed(or_1_out), .Instruction__10_6(Instruction__15_0[10:6]),
    .Input_1(Read_Data_1), .Input_2(multiplexer_1_out), .Output(slu_1_output));
  MDLU mdlu_1 (
    .OPCode(alu_decoder_1_operation), .Input_1(Read_Data_1), .Input_2(multiplexer_1_out), .Signed(or_1_out),
    .HI(mdlu_1_hi), .LO(mdlu_1_lo));
  and M_D (M_D_out, alu_decoder_1_destination_unit[0], alu_decoder_1_destination_unit[1], ~alu_decoder_1_destination_unit[2]);  // AND_Gate
  and MF_H_L (MF_H_L_out, ~alu_decoder_1_destination_unit[0], alu_decoder_1_destination_unit[1], ~alu_decoder_1_destination_unit[2]);  // AND_Gate
  Multiplexer #(.width(32), .enable("false")) multiplexer_3 (
    .in0(HI_q), .in1(LO_q), .out(multiplexer_3_out), .sel(alu_decoder_1_operation[0]));
  Register #(.width(32), .trigger("high")) HI (.D(mdlu_1_hi), .en(or_2_out), .Q(HI_q), .clk(M_D_out), .clr(1'b0));
  Register #(.width(32), .trigger("high")) LO (.D(mdlu_1_lo), .en(or_2_out), .Q(LO_q), .clk(M_D_out), .clr(1'b0));
  or or_2 (or_2_out, M_D_out, MF_H_L_out);
  Multiplexer #(.select(3), .width(32), .enable("false")) multiplexer_4 (
    .in0(slu_1_output), .in2(multiplexer_3_out), .in3({32{1'b0}}), .in4(alu_1_result), .in5(alu_1_result),
    .out(Result), .sel(alu_decoder_1_destination_unit));  // open: in1, in6, in7
  // Probe on alu_decoder_1_destination_unit
  Zero zero_1 (.Input(Result), .Zero(Zero));
  Multiplexer #(.enable("false")) multiplexer_5 (.in0(alu_1_overflow), .in1(1'b0), .out(Overflow), .sel(and_1_out));
  and and_1 (and_1_out, 1'b1, ~alu_decoder_1_destination_unit[1], alu_decoder_1_destination_unit[2]);  // AND_Gate

  // Notes on the sheet:
  //   ALUSrc
  //   RegDst
endmodule

module Control (
  input  [5:0] Instruction__31_26,
  output I_Format,
  output [1:0] ALUOp,
  output [1:0] EX,
  output [2:0] M,
  output [1:0] WB,
  output [2:0] Other
);

  wire and_1_out, and_2_out, and_3_out, and_4_out, and_5_out, and_6_out, and_7_out, and_8_out, and_9_out,
       and_10_out, and_11_out, demultiplexer_1_out1, demultiplexer_1_out3, nor_1_out, or_2_out, or_3_out;

  nor nor_1 (nor_1_out, Instruction__31_26[0], Instruction__31_26[1], Instruction__31_26[2], Instruction__31_26[4], Instruction__31_26[5], Instruction__31_26[3]);
  and and_1 (and_1_out, Instruction__31_26[5], ~Instruction__31_26[3], ~Instruction__31_26[2]);  // AND_Gate
  and and_2 (and_2_out, ~Instruction__31_26[5], Instruction__31_26[3], Instruction__31_26[2]);  // AND_Gate
  and and_3 (and_3_out, ~Instruction__31_26[5], Instruction__31_26[3], ~Instruction__31_26[2]);  // AND_Gate
  and and_4 (and_4_out, ~Instruction__31_26[5], ~Instruction__31_26[3], Instruction__31_26[2]);  // AND_Gate
  and and_5 (and_5_out, Instruction__31_26[5], Instruction__31_26[3], ~Instruction__31_26[2]);  // AND_Gate
  and and_6 (and_6_out, ~Instruction__31_26[5], ~Instruction__31_26[3], ~Instruction__31_26[2]);  // AND_Gate
  or or_1 (I_Format, and_2_out, and_3_out);
  Demultiplexer #(.select(2), .enable("false")) demultiplexer_1 (
    .out1(demultiplexer_1_out1), .out3(demultiplexer_1_out3), .in(and_3_out),
    .sel({Instruction__31_26[0], Instruction__31_26[1]}));  // open: out0, out2
  and and_7 (and_7_out, and_4_out, ~Instruction__31_26[0]);  // AND_Gate
  and and_8 (and_8_out, Instruction__31_26[1], Instruction__31_26[0]);
  and and_9 (and_9_out, Instruction__31_26[1], ~Instruction__31_26[0]);  // AND_Gate
  assign {WB, M, EX, ALUOp} = and_1_out ? 9'h1a4 : 9'bz;  // Controlled_Buffer controlled_buffer_1
  assign {WB, M, EX, ALUOp} = I_Format ? 9'h18e : 9'bz;  // Controlled_Buffer controlled_buffer_2
  assign {WB, M, EX, ALUOp} = and_4_out ? 9'h11 : 9'bz;  // Controlled_Buffer controlled_buffer_3
  assign {WB, M, EX, ALUOp} = and_5_out ? 9'h48 : 9'bz;  // Controlled_Buffer controlled_buffer_4
  and and_10 (and_10_out, and_6_out, and_8_out);
  and and_11 (and_11_out, and_6_out, and_9_out);
  assign {WB, M, EX, ALUOp} = or_2_out ? {9{1'b0}} : 9'bz;  // Controlled_Buffer controlled_buffer_5
  or or_2 (or_2_out, and_10_out, and_11_out);
  assign {WB, M, EX, ALUOp} = nor_1_out ? 9'h10a : 9'bz;  // Controlled_Buffer controlled_buffer_6
  or or_3 (or_3_out, demultiplexer_1_out1, demultiplexer_1_out3);
  Multiplexer #(.enable("false")) multiplexer_1 (.in0(1'b0), .in1(1'b1), .out(Other[0]), .sel(or_3_out));
  Multiplexer #(.enable("false")) multiplexer_2 (.in0(1'b0), .in1(1'b1), .out(Other[1]), .sel(and_7_out));
  Multiplexer #(.enable("false")) multiplexer_3 (.in0(1'b0), .in1(1'b1), .out(Other[2]), .sel(or_2_out));

  // Notes on the sheet:
  //   Book: Pg. 360
  //   R-Type
  //   LW
  //   BEQ/BNE
  //   SW
  //   J/JAL
  //   ANDI/LUI/ORI/XORI
  //   ADDI/ADDIU/SLTI/SLTIU
  //   J
  //   JAL
  //   signed
  //   BEQ/BNE
  //   Jump
  //   0 - RegDst
  //   1 - ALUSrc
  //   0 - Branch
  //   1 - MemRead
  //   0 - MemtoReg
  //   1 - RegWrite
  //   0 - Signed
  //   2 - Jump
  //   2 - MemWrite
  //   1 - 0:BNE/1:BEQ
endmodule

module ALU (
  input  [3:0] OPCode,
  input  [31:0] Input_1,
  input  [31:0] Input_2,
  output [31:0] Result,
  output Overflow
);

  wire n4bit_alu_1_carryout, n4bit_alu_2_carryout, n4bit_alu_3_carryout, n4bit_alu_4_carryout,
       n4bit_alu_5_carryout, n4bit_alu_6_carryout, n4bit_alu_7_carryout, n4bit_alu_8_carryout;

  _4bit_ALU u_4bit_alu_1 (
    .a0(Input_1[0]), .b0(Input_2[0]), .a1(Input_1[1]), .b1(Input_2[1]), .a2(Input_1[2]), .b2(Input_2[2]),
    .a3(Input_1[3]), .b3(Input_2[3]), .AInvert(OPCode[3]), .Binvert(OPCode[2]), .High_Order(1'b0),
    .CarryIn(OPCode[2]), .Operation(OPCode[1:0]), .CarryOut(n4bit_alu_1_carryout), .Result(Result[3:0]));  // open: Overflow
  _4bit_ALU u_4bit_alu_2 (
    .a0(Input_1[4]), .b0(Input_2[4]), .a1(Input_1[5]), .b1(Input_2[5]), .a2(Input_1[6]), .b2(Input_2[6]),
    .a3(Input_1[7]), .b3(Input_2[7]), .AInvert(OPCode[3]), .Binvert(OPCode[2]), .High_Order(1'b0),
    .CarryIn(n4bit_alu_1_carryout), .Operation(OPCode[1:0]), .CarryOut(n4bit_alu_2_carryout),
    .Result(Result[7:4]));  // open: Overflow
  _4bit_ALU u_4bit_alu_3 (
    .a0(Input_1[8]), .b0(Input_2[8]), .a1(Input_1[9]), .b1(Input_2[9]), .a2(Input_1[10]), .b2(Input_2[10]),
    .a3(Input_1[11]), .b3(Input_2[11]), .AInvert(OPCode[3]), .Binvert(OPCode[2]), .High_Order(1'b0),
    .CarryIn(n4bit_alu_2_carryout), .Operation(OPCode[1:0]), .CarryOut(n4bit_alu_3_carryout),
    .Result(Result[11:8]));  // open: Overflow
  _4bit_ALU u_4bit_alu_4 (
    .a0(Input_1[12]), .b0(Input_2[12]), .a1(Input_1[13]), .b1(Input_2[13]), .a2(Input_1[14]),
    .b2(Input_2[14]), .a3(Input_1[15]), .b3(Input_2[15]), .AInvert(OPCode[3]), .Binvert(OPCode[2]),
    .High_Order(1'b0), .CarryIn(n4bit_alu_3_carryout), .Operation(OPCode[1:0]),
    .CarryOut(n4bit_alu_4_carryout), .Result(Result[15:12]));  // open: Overflow
  _4bit_ALU u_4bit_alu_5 (
    .a0(Input_1[16]), .b0(Input_2[16]), .a1(Input_1[17]), .b1(Input_2[17]), .a2(Input_1[18]),
    .b2(Input_2[18]), .a3(Input_1[19]), .b3(Input_2[19]), .AInvert(OPCode[3]), .Binvert(OPCode[2]),
    .High_Order(1'b0), .CarryIn(n4bit_alu_4_carryout), .Operation(OPCode[1:0]),
    .CarryOut(n4bit_alu_5_carryout), .Result(Result[19:16]));  // open: Overflow
  _4bit_ALU u_4bit_alu_6 (
    .a0(Input_1[20]), .b0(Input_2[20]), .a1(Input_1[21]), .b1(Input_2[21]), .a2(Input_1[22]),
    .b2(Input_2[22]), .a3(Input_1[23]), .b3(Input_2[23]), .AInvert(OPCode[3]), .Binvert(OPCode[2]),
    .High_Order(1'b0), .CarryIn(n4bit_alu_5_carryout), .Operation(OPCode[1:0]),
    .CarryOut(n4bit_alu_6_carryout), .Result(Result[23:20]));  // open: Overflow
  _4bit_ALU u_4bit_alu_7 (
    .a0(Input_1[24]), .b0(Input_2[24]), .a1(Input_1[25]), .b1(Input_2[25]), .a2(Input_1[26]),
    .b2(Input_2[26]), .a3(Input_1[27]), .b3(Input_2[27]), .AInvert(OPCode[3]), .Binvert(OPCode[2]),
    .High_Order(1'b0), .CarryIn(n4bit_alu_6_carryout), .Operation(OPCode[1:0]),
    .CarryOut(n4bit_alu_7_carryout), .Result(Result[27:24]));  // open: Overflow
  _4bit_ALU u_4bit_alu_8 (
    .a0(Input_1[28]), .b0(Input_2[28]), .a1(Input_1[29]), .b1(Input_2[29]), .a2(Input_1[30]),
    .b2(Input_2[30]), .a3(Input_1[31]), .b3(Input_2[31]), .AInvert(OPCode[3]), .Binvert(OPCode[2]),
    .High_Order(1'b1), .CarryIn(n4bit_alu_7_carryout), .Operation(OPCode[1:0]),
    .CarryOut(n4bit_alu_8_carryout), .Result(Result[31:28]), .Overflow(Overflow));
endmodule

// Decoder
module ALU_Decoder (
  input  [5:0] Funct__5_0,
  input  I_Format,
  input  [31:0] Instruction__31_26,
  output [3:0] Operation,
  output Signed,
  output [2:0] Destination_Unit
);

  wire [4:0] multiplexer_1_out, multiplexer_2_out, multiplexer_3_out, multiplexer_4_out, multiplexer_5_out,
       multiplexer_6_out;

  // Probe on Funct__5_0[2:0]
  // Probe on Funct__5_0[5:3]
  Multiplexer #(.select(3), .width(5), .enable("false")) multiplexer_1 (
    .in0(5'b00010), .in2({5{1'b0}}), .in3(5'b10000), .in4(5'b00011), .in6(5'b00001), .out(multiplexer_1_out),
    .sel(Funct__5_0[2:0]));  // open: in1, in5, in7
  // AND_Gate and_1 has open pins: in0=Instruction__31_26[3], in1=Instruction__31_26[2], out=open
  Multiplexer #(.select(3), .width(5), .enable("false")) multiplexer_2 (
    .in0({5{1'b0}}), .out(multiplexer_2_out), .sel(Funct__5_0[2:0]));  // open: in1, in2, in3, in4, in5, in6, in7
  Multiplexer #(.select(3), .width(5), .enable("false")) multiplexer_3 (
    .in0({5{1'b0}}), .in2(5'b00001), .out(multiplexer_3_out), .sel(Funct__5_0[2:0]));  // open: in1, in3, in4, in5, in6, in7
  Multiplexer #(.select(3), .width(5), .enable("false")) multiplexer_4 (
    .in0(5'b10001), .in1(5'b00001), .in2(5'b10000), .in3({5{1'b0}}), .out(multiplexer_4_out),
    .sel(Funct__5_0[2:0]));  // open: in4, in5, in6, in7
  Multiplexer #(.select(3), .width(5), .enable("false")) multiplexer_5 (
    .in0(5'b00010), .in1(5'b10010), .in2(5'b00110), .in3(5'b10110), .in4({5{1'b0}}), .in5(5'b00001),
    .in7(5'b00101), .out(multiplexer_5_out), .sel(Funct__5_0[2:0]));  // open: in6
  Multiplexer #(.select(3), .width(5), .enable("false")) multiplexer_6 (
    .in2(5'b10111), .in3(5'b00111), .out(multiplexer_6_out), .sel(Funct__5_0[2:0]));  // open: in0, in1, in4, in5, in6, in7
  Multiplexer #(.select(3), .width(5), .enable("false")) multiplexer_7 (
    .in0(multiplexer_1_out), .in1(multiplexer_2_out), .in2(multiplexer_3_out), .in3(multiplexer_4_out),
    .in4(multiplexer_5_out), .in5(multiplexer_6_out), .out({Signed, Operation}), .sel(Funct__5_0[5:3]));  // open: in6, in7

  assign Destination_Unit = Funct__5_0[5:3];

  // Notes on the sheet:
  //   Shift
  //   SLL
  //   SRL
  //   SRA
  //   SLLV
  //   SRLV
  //   JR
  //   JR
  //   HI
  //   LO
  //   Move
  //   MULT
  //   MULTU
  //   DIV
  //   DIVU
  //   Mult/Div
  //   ADD
  //   ADDU
  //   SUB
  //   SUBU
  //   AND
  //   OR
  //   NOR
  //   ALU
  //   SLTU
  //   SLT
  //   SLT
endmodule

module _1bit_ALU (
  input  AInvert,
  input  BInvert,
  input  CarryIn,
  input  [1:0] Operation,
  input  A,
  input  B,
  input  Less,
  output Output,
  output CarryOut
);

  wire adder_1_out, and_1_out, multiplexer_1_out, multiplexer_2_out, not_1_out, not_2_out, or_1_out;

  Multiplexer #(.enable("false")) multiplexer_1 (.in0(A), .in1(not_1_out), .out(multiplexer_1_out), .sel(AInvert));
  not not_1 (not_1_out, A);
  Multiplexer #(.enable("false")) multiplexer_2 (.in0(B), .in1(not_2_out), .out(multiplexer_2_out), .sel(BInvert));
  not not_2 (not_2_out, B);
  and and_1 (and_1_out, multiplexer_1_out, multiplexer_2_out);
  or or_1 (or_1_out, multiplexer_1_out, multiplexer_2_out);
  Adder #(.width(1)) adder_1 (
    .a(multiplexer_1_out), .b(multiplexer_2_out), .out(adder_1_out), .cin(CarryIn), .cout(CarryOut));
  Multiplexer #(.select(2), .enable("false")) multiplexer_3 (
    .in0(and_1_out), .in1(or_1_out), .in2(adder_1_out), .in3(Less), .out(Output), .sel(Operation));
endmodule

// 4-Bit ALU
module _4bit_ALU (
  input  CarryIn,
  input  [1:0] Operation,
  input  a0,
  input  b0,
  input  a1,
  input  b1,
  input  a2,
  input  b2,
  input  a3,
  input  b3,
  input  AInvert,
  input  Binvert,
  input  High_Order,
  output [3:0] Result,
  output Overflow,
  output CarryOut
);

  wire n1bit_alu_1_carryout, n1bit_alu_2_carryout, n1bit_alu_3_carryout, n1bit_alu_high_1_carryout,
       n1bit_alu_high_1_overflow, n1bit_alu_high_1_set;

  _1bit_ALU u_1bit_alu_1 (
    .A(a0), .B(b0), .Less(n1bit_alu_high_1_set), .AInvert(AInvert), .BInvert(Binvert), .CarryIn(CarryIn),
    .Operation(Operation), .CarryOut(n1bit_alu_1_carryout), .Output(Result[0]));
  _1bit_ALU u_1bit_alu_2 (
    .A(a1), .B(b1), .Less(1'b0), .AInvert(AInvert), .BInvert(Binvert), .CarryIn(n1bit_alu_1_carryout),
    .Operation(Operation), .CarryOut(n1bit_alu_2_carryout), .Output(Result[1]));
  _1bit_ALU u_1bit_alu_3 (
    .A(a2), .B(b2), .Less(1'b0), .AInvert(AInvert), .BInvert(Binvert), .CarryIn(n1bit_alu_2_carryout),
    .Operation(Operation), .CarryOut(n1bit_alu_3_carryout), .Output(Result[2]));
  _1bit_ALU__High u_1bit_alu_high_1 (
    .A(a3), .B(b3), .Less(1'b0), .AInvert(AInvert), .BInvert(Binvert), .CarryIn(n1bit_alu_3_carryout),
    .Operation(Operation), .CarryOut(n1bit_alu_high_1_carryout), .Output(Result[3]),
    .Set(n1bit_alu_high_1_set), .Overflow(n1bit_alu_high_1_overflow));
  and and_1 (CarryOut, n1bit_alu_high_1_carryout, ~High_Order);  // AND_Gate
  and and_2 (Overflow, n1bit_alu_high_1_overflow, High_Order);
endmodule

// 1bit ALU
module _1bit_ALU__High (
  input  AInvert,
  input  BInvert,
  input  CarryIn,
  input  [1:0] Operation,
  input  A,
  input  B,
  input  Less,
  output Output,
  output Set,
  output Overflow,
  output CarryOut
);

  wire and_1_out, multiplexer_1_out, multiplexer_2_out, not_1_out, not_2_out, or_1_out;

  Multiplexer #(.enable("false")) multiplexer_1 (.in0(A), .in1(not_1_out), .out(multiplexer_1_out), .sel(AInvert));
  not not_1 (not_1_out, A);
  Multiplexer #(.enable("false")) multiplexer_2 (.in0(B), .in1(not_2_out), .out(multiplexer_2_out), .sel(BInvert));
  not not_2 (not_2_out, B);
  and and_1 (and_1_out, multiplexer_1_out, multiplexer_2_out);
  or or_1 (or_1_out, multiplexer_1_out, multiplexer_2_out);
  Adder #(.width(1)) adder_1 (.a(multiplexer_1_out), .b(multiplexer_2_out), .out(Set), .cin(CarryIn), .cout(CarryOut));
  Multiplexer #(.select(2), .enable("false")) multiplexer_3 (
    .in0(and_1_out), .in1(or_1_out), .in2(Set), .in3(Less), .out(Output), .sel(Operation));
  xor xor_1 (Overflow, CarryOut, CarryIn);
endmodule

// LED
module LED_Toggle (
  input  Reset,
  input  Input,
  output LED
);

  wire and_1_out;

  T_Flip_Flop t_ff_1 (.clk(and_1_out), .T(and_1_out), .Q(LED), .reset(Reset));  // open: Qn, preset, en
  and and_1 (and_1_out, Input, ~LED);  // AND_Gate
endmodule

module SLU (
  input  [3:0] OPCode,
  input  Signed,
  input  [4:0] Instruction__10_6,
  input  [31:0] Input_1,
  input  [31:0] Input_2,
  output [31:0] Output
);

  wire [4:0] multiplexer_1_out;
  wire [31:0] shifter_1_out, shifter_2_out, shifter_3_out;

  Multiplexer #(.width(5), .enable("false")) multiplexer_1 (
    .in0(Instruction__10_6), .in1(Input_2[4:0]), .out(multiplexer_1_out), .sel(OPCode[0]));
  Shifter #(.width(32), .shift("lr")) shifter_1 (.in(Input_1), .\dist (multiplexer_1_out), .out(shifter_1_out));
  Shifter #(.width(32), .shift("ar")) shifter_2 (.in(Input_1), .\dist (multiplexer_1_out), .out(shifter_2_out));
  Shifter #(.width(32)) shifter_3 (.in(Input_1), .\dist (multiplexer_1_out), .out(shifter_3_out));
  Multiplexer #(.select(2), .width(32), .enable("false")) multiplexer_2 (
    .in0(shifter_1_out), .in1(shifter_2_out), .in2(shifter_3_out), .out(Output), .sel({OPCode[1], Signed}));  // open: in3
  // Probe on {OPCode[1], Signed}

  // Notes on the sheet:
  //   Variable
  //   Left
endmodule

module MDLU (
  input  [3:0] OPCode,
  input  [31:0] Input_1,
  input  [31:0] Input_2,
  input  Signed,
  output [31:0] HI,
  output [31:0] LO
);

  wire [30:0] adder_1_out, adder_2_out, controlled_inverter_1_out, controlled_inverter_2_out, divider_2_out,
       divider_2_rem, multiplexer_1_out, multiplexer_2_out, multiplexer_3_out, multiplexer_4_out,
       multiplexer_8_out, multiplier_2_cout, multiplier_2_out;
  wire [31:0] divider_1_out, divider_1_rem, multiplexer_5_out, multiplexer_6_out, multiplexer_7_out,
       multiplier_1_cout, multiplier_1_out;

  Divider #(.width(32)) divider_1 (.a(Input_1), .b(Input_2), .out(divider_1_out), .rem(divider_1_rem));  // open: upper
  Multiplier #(.width(32)) multiplier_1 (
    .a(Input_1), .b(Input_2), .out(multiplier_1_out), .cout(multiplier_1_cout));  // open: cin
  Multiplexer #(.width(31), .enable("false")) multiplexer_1 (
    .in0(Input_1[30:0]), .in1(controlled_inverter_1_out), .out(multiplexer_1_out), .sel(Input_1[31]));
  assign controlled_inverter_1_out = Input_1[31] ? ~Input_1[30:0] : 31'bz;  // Controlled_Inverter controlled_inverter_1
  Multiplexer #(.width(31), .enable("false")) multiplexer_2 (
    .in0(Input_2[30:0]), .in1(controlled_inverter_2_out), .out(multiplexer_2_out), .sel(Input_2[31]));
  assign controlled_inverter_2_out = Input_2[31] ? ~Input_2[30:0] : 31'bz;  // Controlled_Inverter controlled_inverter_2
  Adder #(.width(31)) adder_1 (.a(multiplexer_1_out), .b(31'h1), .out(adder_1_out));  // open: cin, cout
  Adder #(.width(31)) adder_2 (.a(multiplexer_2_out), .b(31'h1), .out(adder_2_out));  // open: cin, cout
  Multiplexer #(.width(31), .enable("false")) multiplexer_3 (
    .in0(multiplexer_1_out), .in1(adder_1_out), .out(multiplexer_3_out), .sel(Input_1[31]));
  Multiplexer #(.width(31), .enable("false")) multiplexer_4 (
    .in0(multiplexer_2_out), .in1(adder_2_out), .out(multiplexer_4_out), .sel(Input_2[31]));
  xor xor_1 (multiplexer_7_out[31], Input_1[31], Input_2[31]);
  Divider #(.width(31)) divider_2 (
    .a(multiplexer_3_out), .b(multiplexer_4_out), .out(divider_2_out), .rem(divider_2_rem));  // open: upper
  Multiplier #(.width(31)) multiplier_2 (
    .a(multiplexer_3_out), .b(multiplexer_4_out), .out(multiplier_2_out), .cout(multiplier_2_cout));  // open: cin
  Multiplexer #(.width(32), .enable("false")) multiplexer_5 (
    .in0(divider_1_out), .in1(multiplier_1_cout), .out(multiplexer_5_out), .sel(OPCode[0]));
  Multiplexer #(.width(32), .enable("false")) multiplexer_6 (
    .in0(divider_1_rem), .in1(multiplier_1_out), .out(multiplexer_6_out), .sel(OPCode[0]));
  Multiplexer #(.width(31), .enable("false")) multiplexer_7 (
    .in0(divider_2_out), .in1(multiplier_2_cout), .out(multiplexer_7_out[30:0]), .sel(OPCode[0]));
  Multiplexer #(.width(31), .enable("false")) multiplexer_8 (
    .in0(divider_2_rem), .in1(multiplier_2_out), .out(multiplexer_8_out), .sel(OPCode[0]));
  Multiplexer #(.width(32), .enable("false")) multiplexer_9 (
    .in0(multiplexer_5_out), .in1(multiplexer_7_out), .out(HI), .sel(Signed));
  Multiplexer #(.width(32), .enable("false")) multiplexer_10 (
    .in0(multiplexer_6_out), .in1({multiplexer_7_out[31], multiplexer_8_out}), .out(LO), .sel(Signed));
endmodule

module Zero (
  input  [31:0] Input,
  output Zero
);

  and and_1 (Zero, Input[0], Input[1], Input[2], Input[3], Input[4], Input[5], Input[6], Input[7], Input[8], Input[9], Input[10], Input[11], Input[12], Input[13], Input[14], Input[15], Input[17], Input[18], Input[19], Input[20], Input[21], Input[22], Input[23], Input[24], Input[25], Input[26], Input[27], Input[28], Input[29], Input[30], Input[31], Input[16]);
endmodule
